// Logisim project ex2-test.circ as structural Verilog: 1 circuit, main circuit main
module main (
  output halt,
  output [7:0] CYCLE,
  output [7:0] ADD_OUT,
  output [7:0] REG_OUT
);

  wire clock_1_out;
  wire [7:0] adder_1_out;

  Comparator comparator_1 (.a(8'hf), .b(CYCLE), .eq(halt));  // open: gt, lt
  Register register_1 (.D(adder_1_out), .clk(clock_1_out), .Q(CYCLE));  // open: en, clr
  Adder adder_1 (.a(CYCLE), .b(8'h1), .out(adder_1_out));  // open: cin, cout
  Clock clock_1 (.out(clock_1_out));
  // AddMachine addmachine_1: pin names not known; wires that end beside it: clock_1_out, ADD_OUT, REG_OUT
endmodule
