// Logisim project ex4-test.circ as structural Verilog: 1 circuit, main circuit main
module main (
  output halt,
  output [1:0] CYCLE,
  output [7:0] SPLIT_IN,
  output SPLIT_OUT0,
  output [7:0] SPLIT_OUT1
);

  wire clock_1_out;
  wire [1:0] adder_1_out;

  Comparator #(.width(2)) comparator_1 (.a(2'b11), .b(CYCLE), .eq(halt));  // open: gt, lt
  Register #(.width(2)) register_1 (.D(adder_1_out), .clk(clock_1_out), .Q(CYCLE));  // open: en, clr
  Adder #(.width(2)) adder_1 (.a(CYCLE), .b(2'b01), .out(adder_1_out));  // open: cin, cout
  Clock clock_1 (.out(clock_1_out));
  ROM #(.addrWidth(2)) rom_1 (.addr(CYCLE), .data(SPLIT_IN));
  // SplitThing splitthing_1: pin names not known; wires that end beside it: SPLIT_IN, SPLIT_OUT0, SPLIT_OUT1

  // Notes on the sheet:
  //   contents of rom_1 (hex, n*v repeats v):
  //   1 82 a1 5a
endmodule
